// Logisim project processor_singlecycle.circ as structural Verilog: 7 circuits, main circuit CPU_8_BIT
module CPU_8_BIT (
  input  rst
);

  wire and_1_out, and_2_out, and_4_out, and_5_out, bcd_to_7_segment_decoder_2_p1,
       bcd_to_7_segment_decoder_3_p1, bcd_to_7_segment_decoder_6_p1, bcd_to_7_segment_decoder_9_p1,
       bcd_to_7_segment_decoder_11_p1, bcd_to_7_segment_decoder_12_p1, binary_to_bcd_converter_1_p2,
       binary_to_bcd_converter_2_p3, binary_to_bcd_converter_2_p5, binary_to_bcd_converter_3_p2,
       binary_to_bcd_converter_3_p4, binary_to_bcd_converter_4_p3, button_1_out, button_2_out, c_cond,
       c_flag, call, clk, clock_1_out, comparator_1_eq, comparator_2_gt, decoder_1_out0, decoder_1_out1,
       decoder_1_out2, decoder_1_out3, decoder_1_out4, decoder_1_out5, decoder_1_out6, mem_write_en,
       mux_load_imm, mux_pc_branch, mux_reg_mem_write, mux_skip_alu_out, not_1_out, or_1_out, or_2_out,
       or_5_out, pc_en, reg_write_en, ret, rgb_video_1_p1, rgb_video_1_p3, rst_t, z_flag;
  wire [2:0] multiplexer_10_out;
  wire [2:2] register_file_16_x_8_1_read_data1_o;
  wire [3:0] alu_opcode;
  wire [4:0] adder_2_out, multiplexer_1_out, multiplexer_4_out, multiplexer_9_out, register_1_q,
       subtractor_1_out;
  wire [5:2] Instruction_Memory_data_2;
  wire [6:0] rgb_video_1_p4, rgb_video_1_p5, rgb_video_1_p6;
  wire [7:0] alu_8_bit_1_y_o, binary_to_bcd_converter_1_p1, binary_to_bcd_converter_2_p2,
       binary_to_bcd_converter_3_p1, binary_to_bcd_converter_4_p2, Data_Memory_dout, multiplexer_5_out,
       multiplexer_6_out, multiplexer_7_out, multiplexer_8_out, register_file_16_x_8_1_read_data0_o;
  wire [7:7] vid_xpos_q, vid_ypos_q;
  wire [9:0] adder_1_out, Function_Call_Stack_dout, Instruction_Memory_data, multiplexer_2_out,
       multiplexer_3_out, PC_q;

  or or_1 (or_1_out, call, ret);
  Adder #(.width(10)) adder_1 (.a(10'h1), .b(PC_q), .out(adder_1_out));  // open: cin, cout
  Multiplexer #(.width(5)) multiplexer_1 (.in0(5'b00001), .in1({5{1'b1}}), .out(multiplexer_1_out), .sel(ret));
  Clock clock_1 (.out(clock_1_out));
  Multiplexer #(.width(10)) multiplexer_2 (
    .in0(adder_1_out), .in1(multiplexer_3_out), .out(multiplexer_2_out), .sel(mux_pc_branch));
  Adder #(.width(5)) adder_2 (.a(register_1_q), .b(multiplexer_1_out), .out(adder_2_out));  // open: cin, cout
  Register #(.width(5)) register_1 (.D(adder_2_out), .en(or_2_out), .clk(clk), .Q(register_1_q), .clr(rst_t));
  or or_2 (or_2_out, call, ret);
  Button button_1 (.out(button_1_out));
  Button button_2 (.out(button_2_out));
  Multiplexer #(.width(10)) multiplexer_3 (
    .in0(Instruction_Memory_data), .in1(Function_Call_Stack_dout), .out(multiplexer_3_out), .sel(ret));
  or or_3 (clk, button_1_out, clock_1_out);
  or or_4 (rst_t, rst, button_2_out);
  Register #(.width(10)) PC (.D(multiplexer_2_out), .en(pc_en), .clk(clk), .Q(PC_q), .clr(rst_t));
  Multiplexer #(.width(5)) multiplexer_4 (
    .in0(register_1_q), .in1(adder_2_out), .out(multiplexer_4_out), .sel(or_1_out));
  Subtractor #(.width(5)) subtractor_1 (
    .a(multiplexer_4_out), .b(5'b00001), .out(subtractor_1_out));  // open: bin, bout
  RAM #(.addrWidth(5), .dataWidth(10)) Function_Call_Stack (
    .addr(subtractor_1_out), .we(call), .oe(1'b1), .clk(clk), .din(adder_1_out),
    .dout(Function_Call_Stack_dout));
  ROM #(.addrWidth(10), .dataWidth(14)) Instruction_Memory (
    .addr(PC_q), .data({Instruction_Memory_data_2, Instruction_Memory_data}));
  TTY #(.rows(10)) tty_1 (.data(rgb_video_1_p6), .clk(clk), .we(decoder_1_out3), .clr(or_5_out));
  Multiplexer #(.width(8)) multiplexer_5 (
    .in0(multiplexer_6_out), .in1({Instruction_Memory_data_2[3:2], Instruction_Memory_data[9:4]}),
    .out(multiplexer_5_out), .sel(mux_load_imm));
  Multiplexer #(.width(8)) multiplexer_6 (
    .in0(multiplexer_7_out), .in1(Data_Memory_dout), .out(multiplexer_6_out), .sel(mux_reg_mem_write));
  or or_5 (or_5_out, and_1_out, rst_t);
  and and_1 (and_1_out, register_file_16_x_8_1_read_data1_o[2], decoder_1_out3);
  CONTROL_UNIT control_unit_1 (
    .opcode({Instruction_Memory_data_2, Instruction_Memory_data[9:8]}), .z_i(z_flag), .c_i(c_flag),
    .clk(clk), .rst(rst_t), .alu_opcode(alu_opcode), .mux_reg_mem_write(mux_reg_mem_write),
    .mux_skip_alu_out(mux_skip_alu_out), .pc_en(pc_en), .reg_write_en(reg_write_en),
    .mux_load_imm(mux_load_imm), .mem_write_en(mem_write_en), .mux_pc_branch(mux_pc_branch), .c_o(c_cond),
    .call_o(call), .ret_o(ret));
  Comparator comparator_1 (.a(multiplexer_5_out), .b({8{1'b0}}), .eq(comparator_1_eq));  // open: gt, lt
  // RGB_Video #(.cursor("No Cursor")) rgb_video_1: pin names not known; wires that end beside it: rgb_video_1_p1, clk, rgb_video_1_p3, rgb_video_1_p4, rgb_video_1_p5, rgb_video_1_p6
  or or_6 (rgb_video_1_p1, rst_t, and_2_out);
  and and_2 (and_2_out, rgb_video_1_p3, register_file_16_x_8_1_read_data1_o[2]);
  // Probe on register_file_16_x_8_1_read_data0_o
  // Probe on {register_file_16_x_8_1_read_data1_o[2], rgb_video_1_p6}
  _7_Segment_Display u_7_segment_display_1 ();  // open: g, f, a, b, e, d, c, dp
  _7_Segment_Display u_7_segment_display_2 ();  // open: g, f, a, b, e, d, c, dp
  // BCD_to_7_Segment_decoder bcd_to_7_segment_decoder_1: pin names not known
  // BCD_to_7_Segment_decoder bcd_to_7_segment_decoder_2: pin names not known; wires that end beside it: bcd_to_7_segment_decoder_2_p1
  // Binary_to_BCD_converter #(.binvalue(8)) binary_to_bcd_converter_1: pin names not known; wires that end beside it: binary_to_bcd_converter_1_p1, binary_to_bcd_converter_1_p2, binary_to_bcd_converter_1_p2, bcd_to_7_segment_decoder_2_p1
  REGISTER_FILE_16_X_8 register_file_16_x_8_1 (
    .clk(clk), .rst(rst_t), .read_addr0_i(Instruction_Memory_data[3:0]),
    .read_addr1_i(Instruction_Memory_data[7:4]), .write_addr(Instruction_Memory_data[3:0]),
    .write_data(multiplexer_5_out), .write_en(reg_write_en),
    .read_data0_o(register_file_16_x_8_1_read_data0_o),
    .read_data1_o({register_file_16_x_8_1_read_data1_o[2], rgb_video_1_p6}));
  and and_3 (z_flag, reg_write_en, comparator_1_eq);
  _7_Segment_Display u_7_segment_display_3 ();  // open: g, f, a, b, e, d, c, dp
  // BCD_to_7_Segment_decoder bcd_to_7_segment_decoder_3: pin names not known; wires that end beside it: bcd_to_7_segment_decoder_3_p1
  _7_Segment_Display u_7_segment_display_4 ();  // open: g, f, a, b, e, d, c, dp
  // BCD_to_7_Segment_decoder bcd_to_7_segment_decoder_4: pin names not known
  // Binary_to_BCD_converter #(.binvalue(8)) binary_to_bcd_converter_2: pin names not known; wires that end beside it: bcd_to_7_segment_decoder_3_p1, binary_to_bcd_converter_2_p2, binary_to_bcd_converter_2_p3, binary_to_bcd_converter_2_p3, binary_to_bcd_converter_2_p5
  _7_Segment_Display u_7_segment_display_5 ();  // open: g, f, a, b, e, d, c, dp
  // BCD_to_7_Segment_decoder bcd_to_7_segment_decoder_5: pin names not known; wires that end beside it: binary_to_bcd_converter_2_p5
  _7_Segment_Display u_7_segment_display_6 ();  // open: g, f, a, b, e, d, c, dp
  // BCD_to_7_Segment_decoder bcd_to_7_segment_decoder_6: pin names not known; wires that end beside it: bcd_to_7_segment_decoder_6_p1, bcd_to_7_segment_decoder_6_p1
  ALU_8_BIT alu_8_bit_1 (
    .d0_o(register_file_16_x_8_1_read_data0_o),
    .d1_o({register_file_16_x_8_1_read_data1_o[2], rgb_video_1_p6}), .alu_op_i(alu_opcode), .c_i(c_cond),
    .y_o(alu_8_bit_1_y_o), .c_o(c_flag));
  _7_Segment_Display u_7_segment_display_7 ();  // open: g, f, a, b, e, d, c, dp
  // BCD_to_7_Segment_decoder bcd_to_7_segment_decoder_7: pin names not known
  // Binary_to_BCD_converter #(.binvalue(8)) binary_to_bcd_converter_3: pin names not known; wires that end beside it: binary_to_bcd_converter_3_p1, binary_to_bcd_converter_3_p2, binary_to_bcd_converter_3_p2, binary_to_bcd_converter_3_p4
  // Probe on alu_8_bit_1_y_o
  _7_Segment_Display u_7_segment_display_8 ();  // open: g, f, a, b, e, d, c, dp
  // BCD_to_7_Segment_decoder bcd_to_7_segment_decoder_8: pin names not known; wires that end beside it: binary_to_bcd_converter_3_p4
  Multiplexer #(.width(8)) multiplexer_7 (
    .in0(alu_8_bit_1_y_o), .in1({register_file_16_x_8_1_read_data1_o[2], rgb_video_1_p6}),
    .out(multiplexer_7_out), .sel(mux_skip_alu_out));
  _7_Segment_Display u_7_segment_display_9 ();  // open: g, f, a, b, e, d, c, dp
  // BCD_to_7_Segment_decoder bcd_to_7_segment_decoder_9: pin names not known; wires that end beside it: bcd_to_7_segment_decoder_9_p1
  _7_Segment_Display u_7_segment_display_10 ();  // open: g, f, a, b, e, d, c, dp
  _7_Segment_Display u_7_segment_display_11 ();  // open: g, f, a, b, e, d, c, dp
  // BCD_to_7_Segment_decoder bcd_to_7_segment_decoder_10: pin names not known
  // BCD_to_7_Segment_decoder bcd_to_7_segment_decoder_11: pin names not known; wires that end beside it: bcd_to_7_segment_decoder_11_p1
  // Binary_to_BCD_converter #(.binvalue(8)) binary_to_bcd_converter_4: pin names not known; wires that end beside it: bcd_to_7_segment_decoder_9_p1, binary_to_bcd_converter_4_p2, binary_to_bcd_converter_4_p3, binary_to_bcd_converter_4_p3, bcd_to_7_segment_decoder_11_p1
  Multiplexer #(.width(8)) multiplexer_8 (
    .in0(register_file_16_x_8_1_read_data0_o),
    .in1({register_file_16_x_8_1_read_data1_o[2], rgb_video_1_p6}), .out(multiplexer_8_out),
    .sel(mux_reg_mem_write));
  Comparator #(.mode("unsigned")) comparator_2 (
    .a(8'h1f), .b(multiplexer_8_out), .gt(comparator_2_gt));  // open: eq, lt
  Multiplexer #(.width(5)) multiplexer_9 (
    .in0(register_file_16_x_8_1_read_data0_o[4:0]), .in1(rgb_video_1_p6[4:0]), .out(multiplexer_9_out),
    .sel(mux_reg_mem_write));
  Multiplexer #(.width(3)) multiplexer_10 (
    .in0(register_file_16_x_8_1_read_data0_o[7:5]),
    .in1({register_file_16_x_8_1_read_data1_o[2], rgb_video_1_p6[6:5]}), .out(multiplexer_10_out),
    .sel(mux_reg_mem_write));
  _7_Segment_Display u_7_segment_display_12 ();  // open: g, f, a, b, e, d, c, dp
  // BCD_to_7_Segment_decoder bcd_to_7_segment_decoder_12: pin names not known; wires that end beside it: bcd_to_7_segment_decoder_12_p1, bcd_to_7_segment_decoder_12_p1
  and and_4 (and_4_out, comparator_2_gt, mem_write_en);
  RAM #(.addrWidth(5), .asyncread("true")) Data_Memory (
    .addr(multiplexer_9_out), .we(and_4_out), .oe(1'b1), .clk(clk),
    .din({register_file_16_x_8_1_read_data1_o[2], rgb_video_1_p6}), .dout(Data_Memory_dout));
  not not_1 (not_1_out, comparator_2_gt);
  and and_5 (and_5_out, not_1_out, mem_write_en);
  Decoder #(.select(3)) decoder_1 (
    .out0(decoder_1_out0), .out1(decoder_1_out1), .out2(decoder_1_out2), .out3(decoder_1_out3),
    .out4(decoder_1_out4), .out5(decoder_1_out5), .out6(decoder_1_out6), .out7(rgb_video_1_p3),
    .sel(multiplexer_10_out), .en(and_5_out));
  Register bcd0 (
    .D({register_file_16_x_8_1_read_data1_o[2], rgb_video_1_p6}), .en(decoder_1_out0), .clk(clk),
    .Q(binary_to_bcd_converter_1_p1), .clr(rst_t));
  Register bcd1 (
    .D({register_file_16_x_8_1_read_data1_o[2], rgb_video_1_p6}), .en(decoder_1_out1), .clk(clk),
    .Q(binary_to_bcd_converter_2_p2), .clr(rst_t));
  Register bcd2 (
    .D({register_file_16_x_8_1_read_data1_o[2], rgb_video_1_p6}), .en(decoder_1_out2), .clk(clk),
    .Q(binary_to_bcd_converter_3_p1), .clr(rst_t));
  Register bcd3 (
    .D({register_file_16_x_8_1_read_data1_o[2], rgb_video_1_p6}), .en(decoder_1_out4), .clk(clk),
    .Q(binary_to_bcd_converter_4_p2), .clr(rst_t));
  Register vid_xpos (
    .D({register_file_16_x_8_1_read_data1_o[2], rgb_video_1_p6}), .en(decoder_1_out5), .clk(clk),
    .Q({vid_xpos_q[7], rgb_video_1_p4}), .clr(rst_t));
  Register vid_ypos (
    .D({register_file_16_x_8_1_read_data1_o[2], rgb_video_1_p6}), .en(decoder_1_out6), .clk(clk),
    .Q({vid_ypos_q[7], rgb_video_1_p5}), .clr(rst_t));

  // Notes on the sheet:
  //   contents of Instruction_Memory (hex, n*v repeats v):
  //   2011 21e3 4d6 3007 3002 3652 1026 3002 3662 1026 3052 3662 1c10 3052 3065 3026 3002 3662 1028 3457
  //   3616 410 3007 3002 3652 1026 3002 3662 1026 3052 3662 1828 3665 3417 3052 3602 1028 41d 2007 800 800
  //   2417 4a9 2427 4a9 2437 4a9 2447 4a9 2457 4a9 2467 4a9 2477 4a9 2487 4a9 2497 4a9 24a7 4a9 24b7 4a9
  //   24c7 4a9 24d7 4a9 24e7 4a9 24f7 4a9 2507 4a9 2517 4a9 2527 4a9 2537 4a9 2547 4a9 2557 4a9 2567 4a9
  //   2577 4a9 2587 4a9 2597 4a9 25a7 4a9 2207 4a9 2217 4a9 2227 4a9 2237 4a9 2247 4a9 2257 4a9 2267 4a9
  //   2277 4a9 2287 4a9 2297 4a9 22a7 4a9 22b7 4a9 22c7 4a9 22d7 4a9 22e7 4a9 22f7 4a9 23a7 4a9 23b7 4a9
  //   23c7 4a9 23d7 4a9 23e7 4a9 23f7 4a9 2407 4a9 20a7 4a9 2307 4a9 2317 4a9 2327 4a9 2337 4a9 2347 4a9
  //   2357 4a9 2367 4a9 2377 4a9 2387 4a9 2397 4a9 22b7 4a9 22d7 4a9 22f7 4a9 22a7 4a9 27f2 c72 800 27f2
  //   2807 c72 800 c53 3613 c63 3613 c73 3613 200a 20a6 3075 3072 3602 10c2 16 c53 3613 3075 341a 4b9 30a2
  //   3602 108d 3413 3c37 2302 3427 27f2 c72 361a 30a2 3602 14c5 3413 3c37 3413 3c36 3413 3c35 800 37 31
  //   3f 3f 45 5d 55 45 4b 3f 2f 5f 8b 2277 3075 b0 5d a7 5d 2067 3076 b0 5d 83 5d 3 b0 8b 2ff7 3075 b0 5d
  //   a5 5d 22f7 3076 b0 5d 83 5d 16 b0 75 5d 4b 31 41 7d 5d 3057 b0 509
  //   term_data
  //   vid_color
endmodule

module REGISTER_FILE_8_X_8 (
  input  clk,
  input  rst,
  input  [2:0] read_addr0_i,
  input  [2:0] read_addr1_i,
  input  [2:0] write_addr,
  input  [7:0] write_data,
  input  write_en,
  output [7:0] read_data0_o,
  output [7:0] read_data1_o
);

  wire decoder_1_out0, decoder_1_out1, decoder_1_out2, decoder_1_out3, decoder_1_out4, decoder_1_out5,
       decoder_1_out6, decoder_1_out7;
  wire [7:0] register_1_q, register_2_q, register_3_q, register_4_q, register_5_q, register_6_q,
       register_7_q, register_8_q;

  Decoder #(.select(3)) decoder_1 (
    .out0(decoder_1_out0), .out1(decoder_1_out1), .out2(decoder_1_out2), .out3(decoder_1_out3),
    .out4(decoder_1_out4), .out5(decoder_1_out5), .out6(decoder_1_out6), .out7(decoder_1_out7),
    .sel(write_addr), .en(write_en));
  Register register_1 (.D(write_data), .en(decoder_1_out0), .clk(clk), .Q(register_1_q), .clr(rst));
  Register register_2 (.D(write_data), .en(decoder_1_out1), .clk(clk), .Q(register_2_q), .clr(rst));
  Register register_3 (.D(write_data), .en(decoder_1_out2), .clk(clk), .Q(register_3_q), .clr(rst));
  Register register_4 (.D(write_data), .en(decoder_1_out3), .clk(clk), .Q(register_4_q), .clr(rst));
  Register register_5 (.D(write_data), .en(decoder_1_out4), .clk(clk), .Q(register_5_q), .clr(rst));
  Register register_6 (.D(write_data), .en(decoder_1_out5), .clk(clk), .Q(register_6_q), .clr(rst));
  Register register_7 (.D(write_data), .en(decoder_1_out6), .clk(clk), .Q(register_7_q), .clr(rst));
  Register register_8 (.D(write_data), .en(decoder_1_out7), .clk(clk), .Q(register_8_q), .clr(rst));
  Multiplexer #(.select(3), .width(8)) multiplexer_1 (
    .in0(register_1_q), .in1(register_2_q), .in2(register_3_q), .in3(register_4_q), .in4(register_5_q),
    .in5(register_6_q), .in6(register_7_q), .in7(register_8_q), .out(read_data0_o), .sel(read_addr0_i));
  Multiplexer #(.select(3), .width(8)) multiplexer_2 (
    .in0(register_1_q), .in1(register_2_q), .in2(register_3_q), .in3(register_4_q), .in4(register_5_q),
    .in5(register_6_q), .in6(register_7_q), .in7(register_8_q), .out(read_data1_o), .sel(read_addr1_i));
endmodule

module testing (
  input  in_1,
  input  in_2,
  input  [2:0] in_3,
  input  [2:0] in_4,
  input  [2:0] in_5,
  input  [7:0] in_6,
  input  in_7,
  input  in_8,
  input  in_9,
  input  [3:0] in_10,
  input  [3:0] in_11,
  input  [3:0] in_12,
  input  [7:0] in_13,
  input  in_14,
  input  [7:0] in_15,
  input  [7:0] in_16,
  input  [3:0] in_17,
  input  in_18
);

  wire alu_8_bit_1_c_o, undriven, undriven_2, undriven_3;
  wire [7:0] alu_8_bit_1_y_o, register_file_8_x_8_1_read_data0_o, register_file_8_x_8_1_read_data1_o,
       register_file_16_x_8_1_read_data0_o, register_file_16_x_8_1_read_data1_o;

  REGISTER_FILE_8_X_8 register_file_8_x_8_1 (
    .clk(in_1), .rst(in_2), .read_addr0_i(in_3), .read_addr1_i(in_4), .write_addr(in_5), .write_data(in_6),
    .write_en(in_7), .read_data0_o(register_file_8_x_8_1_read_data0_o),
    .read_data1_o(register_file_8_x_8_1_read_data1_o));
  REGISTER_FILE_16_X_8 register_file_16_x_8_1 (
    .clk(in_8), .rst(in_9), .read_addr0_i(in_10), .read_addr1_i(in_11), .write_addr(in_12),
    .write_data(in_13), .write_en(in_14), .read_data0_o(register_file_16_x_8_1_read_data0_o),
    .read_data1_o(register_file_16_x_8_1_read_data1_o));
  ALU_8_BIT alu_8_bit_1 (
    .d0_o(in_15), .d1_o(in_16), .alu_op_i(in_17), .c_i(in_18), .y_o(alu_8_bit_1_y_o), .c_o(alu_8_bit_1_c_o));
  // Probe on alu_8_bit_1_c_o
  // Probe on undriven
  // Probe on register_file_8_x_8_1_read_data0_o
  // Probe on register_file_8_x_8_1_read_data1_o
  // Probe on register_file_16_x_8_1_read_data0_o
  // Probe on register_file_16_x_8_1_read_data1_o
  // Probe on alu_8_bit_1_y_o
  // Probe on undriven_2
  // Probe on undriven_3
endmodule

module REGISTER_FILE_16_X_8 (
  input  clk,
  input  rst,
  input  [3:0] read_addr0_i,
  input  [3:0] read_addr1_i,
  input  [3:0] write_addr,
  input  [7:0] write_data,
  input  write_en,
  output [7:0] read_data0_o,
  output [7:0] read_data1_o
);

  wire decoder_1_out0, decoder_1_out1;
  wire [7:0] register_file_high_read_data0_o, register_file_high_read_data1_o,
       register_file_low_read_data0_o, register_file_low_read_data1_o;

  Decoder decoder_1 (.out0(decoder_1_out0), .out1(decoder_1_out1), .sel(write_addr[3]), .en(write_en));
  REGISTER_FILE_8_X_8 register_file_low (
    .clk(clk), .rst(rst), .read_addr0_i(read_addr0_i[2:0]), .read_addr1_i(read_addr1_i[2:0]),
    .write_addr(write_addr[2:0]), .write_data(write_data), .write_en(decoder_1_out0),
    .read_data0_o(register_file_low_read_data0_o), .read_data1_o(register_file_low_read_data1_o));
  REGISTER_FILE_8_X_8 register_file_high (
    .clk(clk), .rst(rst), .read_addr0_i(read_addr0_i[2:0]), .read_addr1_i(read_addr1_i[2:0]),
    .write_addr(write_addr[2:0]), .write_data(write_data), .write_en(decoder_1_out1),
    .read_data0_o(register_file_high_read_data0_o), .read_data1_o(register_file_high_read_data1_o));
  Multiplexer #(.width(8)) multiplexer_1 (
    .in0(register_file_low_read_data0_o), .in1(register_file_high_read_data0_o), .out(read_data0_o),
    .sel(read_addr0_i[3]));
  Multiplexer #(.width(8)) multiplexer_2 (
    .in0(register_file_low_read_data1_o), .in1(register_file_high_read_data1_o), .out(read_data1_o),
    .sel(read_addr1_i[3]));
endmodule

module ALU_8_BIT (
  input  [7:0] d0_o,
  input  [7:0] d1_o,
  input  [3:0] alu_op_i,
  input  c_i,
  output [7:0] y_o,
  output c_o
);

  wire adder_1_cout, adder_2_cout, and_2_out, and_3_out, and_4_out, and_5_out, and_6_out, decoder_1_out0,
       decoder_1_out1, decoder_1_out2, decoder_1_out3, decoder_1_out13, subtractor_1_bout, subtractor_2_bout;
  wire [7:0] adder_1_out, adder_2_out, and_1_out, not_1_out, or_1_out, shifter_1_out, shifter_2_out,
       shifter_3_out, shifter_4_out, shifter_5_out, shifter_6_out, subtractor_1_out, subtractor_2_out,
       xnor_1_out;

  Decoder #(.enable("false"), .select(4)) decoder_1 (
    .out0(decoder_1_out0), .out1(decoder_1_out1), .out2(decoder_1_out2), .out3(decoder_1_out3),
    .out13(decoder_1_out13), .sel(alu_op_i));  // open: out4, out5, out6, out7, out8, out9, out10, out11, out12, out14, out15
  Adder adder_1 (.a(d0_o), .b(d1_o), .out(adder_1_out), .cout(adder_1_cout));  // open: cin
  Subtractor subtractor_1 (.a(d0_o), .b(d1_o), .out(subtractor_1_out), .bout(subtractor_1_bout));  // open: bin
  Adder adder_2 (.a(d0_o), .b(d1_o), .out(adder_2_out), .cin(c_i), .cout(adder_2_cout));
  Subtractor subtractor_2 (.a(d0_o), .b(d1_o), .out(subtractor_2_out), .bin(c_i), .bout(subtractor_2_bout));
  assign and_1_out = d0_o & d1_o;  // AND_Gate and_1, 8 bits wide
  assign or_1_out = d0_o | d1_o;  // OR_Gate or_1, 8 bits wide
  assign not_1_out = ~d0_o;  // NOT_Gate not_1, 8 bits wide
  assign xnor_1_out = ~(d0_o ^ d1_o);  // XNOR_Gate xnor_1, 8 bits wide
  Shifter #(.shift("ar")) shifter_1 (.in(d0_o), .\dist (3'b001), .out(shifter_1_out));
  Shifter shifter_2 (.in(d0_o), .\dist (3'b001), .out(shifter_2_out));
  Shifter #(.shift("lr")) shifter_3 (.in(d0_o), .\dist (3'b001), .out(shifter_3_out));
  Shifter #(.shift("rl")) shifter_4 (.in(d0_o), .\dist (3'b001), .out(shifter_4_out));
  Shifter #(.shift("rr")) shifter_5 (.in(d0_o), .\dist (3'b001), .out(shifter_5_out));
  Shifter #(.shift("lr")) shifter_6 (.in(d0_o), .\dist (3'b001), .out(shifter_6_out));
  and and_2 (and_2_out, adder_1_cout, decoder_1_out0);
  and and_3 (and_3_out, subtractor_1_bout, decoder_1_out1);
  and and_4 (and_4_out, adder_2_cout, decoder_1_out2);
  and and_5 (and_5_out, subtractor_2_bout, decoder_1_out3);
  and and_6 (and_6_out, d0_o[0], decoder_1_out13);
  Multiplexer #(.select(4), .width(8)) multiplexer_1 (
    .in0(adder_1_out), .in1(subtractor_1_out), .in2(adder_2_out), .in3(subtractor_2_out), .in4(and_1_out),
    .in5(or_1_out), .in6(not_1_out), .in7(xnor_1_out), .in8(shifter_1_out), .in9(shifter_2_out),
    .in10(shifter_3_out), .in11(shifter_4_out), .in12(shifter_5_out), .in13({c_i, shifter_6_out[6:0]}),
    .out(y_o), .sel(alu_op_i));  // open: in14, in15
  or or_2 (c_o, and_2_out, and_3_out, and_4_out, and_5_out, and_6_out);
endmodule

module CONDITION_CODES (
  input  clk,
  input  en,
  input  z_i,
  input  c_i,
  output z_o,
  output c_o
);

  Register #(.width(2)) register_1 (.D({c_i, z_i}), .en(en), .clk(clk), .Q({c_o, z_o}));  // open: clr
endmodule

module CONTROL_UNIT (
  input  [5:0] opcode,
  input  z_i,
  input  c_i,
  input  clk,
  input  rst,
  output [3:0] alu_opcode,
  output mux_reg_mem_write,
  output mux_skip_alu_out,
  output pc_en,
  output reg_write_en,
  output mux_load_imm,
  output mem_write_en,
  output mux_pc_branch,
  output c_o,
  output call_o,
  output ret_o
);

  wire adc, add, and_1_out, and_2_out, and_3_out, and_4_out, and_5_out, and_a, asr, decoder_1_out0,
       decoder_1_out1, decoder_1_out3, decoder_2_out0, decoder_2_out1, decoder_2_out2, decoder_2_out3,
       decoder_2_out4, decoder_2_out5, decoder_2_out6, decoder_2_out7, decoder_2_out13, decoder_2_out14,
       decoder_2_out15, decoder_4_out13, decoder_4_out14, decoder_4_out15, di, ei, goto, jpC, jpNC, jpNZ,
       jpZ, multiplexer_1_out, not_1_out, not_2_out, or_5_out, or_a, priority_encoder_1_p13, reti, rol_a,
       ror_a, rrc, sbc, sub, xnor_a, z_q;

  or or_1 (mux_pc_branch, call_o, goto, ret_o, and_1_out, and_2_out, and_3_out, and_4_out);
  and and_1 (and_1_out, jpZ, z_q);
  and and_2 (and_2_out, jpNZ, not_1_out);
  and and_3 (and_3_out, jpC, c_o);
  and and_4 (and_4_out, jpNC, not_2_out);
  Decoder #(.enable("false"), .select(2)) decoder_1 (
    .out0(decoder_1_out0), .out1(decoder_1_out1), .out2(mux_load_imm), .out3(decoder_1_out3),
    .sel(opcode[5:4]));
  or or_2 (reg_write_en, mux_load_imm, mux_skip_alu_out, xnor_a, or_a, and_a, add, adc, sub, sbc, asr, rrc, ror_a, rol_a, mux_reg_mem_write);
  Decoder #(.select(4)) decoder_2 (
    .out0(decoder_2_out0), .out1(decoder_2_out1), .out2(decoder_2_out2), .out3(decoder_2_out3),
    .out4(decoder_2_out4), .out5(decoder_2_out5), .out6(decoder_2_out6), .out7(decoder_2_out7), .out8(ret_o),
    .out9(reti), .out10(di), .out11(ei), .out12(mem_write_en), .out13(decoder_2_out13),
    .out14(decoder_2_out14), .out15(decoder_2_out15), .sel(opcode[3:0]), .en(decoder_1_out0));
  Decoder #(.select(2)) decoder_3 (
    .out0(jpZ), .out1(jpNZ), .out2(jpC), .out3(jpNC), .sel(opcode[3:2]), .en(decoder_1_out1));
  Decoder #(.select(4)) decoder_4 (
    .out0(mux_skip_alu_out), .out1(xnor_a), .out2(or_a), .out3(and_a), .out4(add), .out5(adc), .out6(sub),
    .out7(sbc), .out8(asr), .out9(rrc), .out10(ror_a), .out11(rol_a), .out12(mux_reg_mem_write),
    .out13(decoder_4_out13), .out14(decoder_4_out14), .out15(decoder_4_out15), .sel(opcode[3:0]),
    .en(decoder_1_out3));
  or or_3 (call_o, decoder_2_out0, decoder_2_out1, decoder_2_out2, decoder_2_out3);
  // OR_Gate or_4 has open pins: in0=decoder_2_out14, in1=decoder_2_out15, out=open
  or or_5 (or_5_out, decoder_4_out14, decoder_4_out15);
  or or_6 (goto, decoder_2_out4, decoder_2_out5, decoder_2_out6, decoder_2_out7);
  D_Flip_Flop z (.D(z_i), .clk(and_5_out), .Q(z_q), .reset(rst));  // open: Qn, preset
  and and_5 (and_5_out, clk, reg_write_en);
  not not_1 (not_1_out, z_q);
  not not_2 (not_2_out, c_o);
  Multiplexer multiplexer_1 (.in0(c_o), .in1(c_i), .out(multiplexer_1_out), .sel(priority_encoder_1_p13));
  D_Flip_Flop c (.D(multiplexer_1_out), .clk(clk), .Q(c_o), .reset(rst));  // open: Qn, preset
  // Priority_Encoder #(.select(4)) priority_encoder_1: pin names not known; wires that end beside it: add, sub, adc, sbc, and_a, or_a, xnor_a, alu_opcode, asr, rol_a, ror_a, rrc, priority_encoder_1_p13
  or or_7 (priority_encoder_1_p13, add, sub, adc, sbc, and_a, or_a, xnor_a, asr, rol_a, ror_a, rrc);

  assign pc_en = 1'b1;

  // Other names for the same wires on the sheet: call = call_o; lw = mux_reg_mem_write; lwi = mux_load_imm;
  //   mov = mux_skip_alu_out; ret = ret_o; sw = mem_write_en
endmodule
